// Logisim project Adding Logic.circ as structural Verilog: 1 circuit, main circuit main
module main (
  input  A,
  input  A2,
  input  B2,
  input  B,
  input  A1,
  input  B1,
  input  A0,
  input  B0,
  output Carry2,
  output Carry,
  output Sum2,
  output Sum,
  output Sum1,
  output Sum0
);

  wire Carry0_out, Carry1_2_out, Carry1_3_out, Carry1_out, Carry2_2_out, Carry2_out, not_1_out, or_1_out,
       Sum1_out, Sum2_out;

  and and_1 (Carry, A, B);
  not not_1 (not_1_out, Carry);
  or or_1 (or_1_out, A, B);
  and and_2 (Sum, not_1_out, or_1_out);
  xor u_Sum1 (Sum1_out, A1, B1);
  and Carry1 (Carry1_out, B1, A1);
  xor u_Sum0 (Sum0, A0, B0);
  and Carry0 (Carry0_out, B0, A0);
  xor Sum1_2 (Sum1, Sum1_out, Carry0_out);
  and Carry1_2 (Carry1_2_out, Sum1_out, Carry0_out);
  xor u_Sum2 (Sum2_out, A2, B2);
  and u_Carry2 (Carry2_out, B2, A2);
  or Carry1_3 (Carry1_3_out, Carry1_2_out, Carry1_out);
  xor Sum2_2 (Sum2, Sum2_out, Carry1_3_out);
  and Carry2_2 (Carry2_2_out, Sum2_out, Carry1_3_out);
  or Carry2_3 (Carry2, Carry2_2_out, Carry2_out);

  // Notes on the sheet:
  //   Half Adder (Adds 2 Bits)
  //   Basically an XOR gate that also outputs a carry from the first AND
  //   Full Adder
endmodule
